// Logisim project MIC-1.circ as structural Verilog: 19 circuits, main circuit main
module main (
  input  CLK,
  output [31:0] PC,
  output [8:0] MPC,
  output [31:0] B,
  output [31:0] C
);

  wire control_unit_1_cpp_b, control_unit_1_cpp_c, control_unit_1_h_c, control_unit_1_lv_b,
       control_unit_1_lv_c, control_unit_1_mar_c, control_unit_1_mbr_b, control_unit_1_mbru_b,
       control_unit_1_mdr_b, control_unit_1_mdr_c, control_unit_1_opc_b, control_unit_1_opc_c,
       control_unit_1_pc_b, control_unit_1_pc_c, control_unit_1_sp_b, control_unit_1_sp_c,
       control_unit_1_tos_b, control_unit_1_tos_c, data_path_1_n, data_path_1_z, RESET_out;
  wire [1:0] control_unit_1_alu_2, control_unit_1_shifter;
  wire [2:0] control_unit_1_mem;
  wire [3:0] control_unit_1_alu;
  wire [7:0] data_path_1_op_code, mem_1_mem_fetch;
  wire [31:0] data_path_1_mem_mar, data_path_1_mem_wr, mem_1_mrm_rd;

  Mem mem_1 (
    .MEM_ADDR_32(data_path_1_mem_mar), .CLK(CLK), .MEM_WR(data_path_1_mem_wr), .MRM_RD(mem_1_mrm_rd),
    .MEM_FETCH(mem_1_mem_fetch), .wr(control_unit_1_mem[2]), .rd(control_unit_1_mem[1]),
    .fetch(control_unit_1_mem[0]), .MEM_ADDR_8(PC));
  Button RESET (.out(RESET_out));
  Data_Path data_path_1 (
    .MEM_WR(data_path_1_mem_wr), .MEM_RD(mem_1_mrm_rd), .rd(control_unit_1_mem[1]),
    .MEM_FETCH(mem_1_mem_fetch), .RESET(RESET_out), .INVA(control_unit_1_alu[1]),
    .ENA(control_unit_1_alu[3]), .CLK(CLK), .ENB(control_unit_1_alu[2]), .INC(control_unit_1_alu[0]),
    .F(control_unit_1_alu_2), .SRA1(control_unit_1_shifter[0]), .SLL8(control_unit_1_shifter[1]),
    .MEM_MAR(data_path_1_mem_mar), .OP_CODE(data_path_1_op_code), .N(data_path_1_n), .Z(data_path_1_z),
    .MAR_C(control_unit_1_mar_c), .MDR_C(control_unit_1_mdr_c), .PC_C(control_unit_1_pc_c),
    .fetch(control_unit_1_mem[0]), .SP_C(control_unit_1_sp_c), .LV_C(control_unit_1_lv_c),
    .CPP_C(control_unit_1_cpp_c), .TOS_C(control_unit_1_tos_c), .OPC_C(control_unit_1_opc_c),
    .H_C(control_unit_1_h_c), .MBR(control_unit_1_mbr_b), .MBRU(control_unit_1_mbru_b),
    .MDR_B(control_unit_1_mdr_b), .PC_B(control_unit_1_pc_b), .SP_B(control_unit_1_sp_b),
    .LV_B(control_unit_1_lv_b), .CPP_B(control_unit_1_cpp_b), .TOS_B(control_unit_1_tos_b),
    .OPC_B(control_unit_1_opc_b), .MEM_PC(PC), .B(B), .C(C));
  Control_Unit control_unit_1 (
    .CLK(CLK), .RESET(RESET_out), .MBR(data_path_1_op_code), .N(data_path_1_n), .Z(data_path_1_z), .MPC(MPC),
    .MDR_B(control_unit_1_mdr_b), .PC_B(control_unit_1_pc_b), .MBR_B(control_unit_1_mbr_b),
    .MBRU_B(control_unit_1_mbru_b), .SP_B(control_unit_1_sp_b), .LV_B(control_unit_1_lv_b),
    .CPP_B(control_unit_1_cpp_b), .TOS_B(control_unit_1_tos_b), .OPC_B(control_unit_1_opc_b),
    .Mem(control_unit_1_mem), .ALU({control_unit_1_alu_2, control_unit_1_alu}),
    .Shifter(control_unit_1_shifter), .H_C(control_unit_1_h_c), .OPC_C(control_unit_1_opc_c),
    .TOS_C(control_unit_1_tos_c), .CPP_C(control_unit_1_cpp_c), .LV_C(control_unit_1_lv_c),
    .SP_C(control_unit_1_sp_c), .PC_C(control_unit_1_pc_c), .MDR_C(control_unit_1_mdr_c),
    .MAR_C(control_unit_1_mar_c));
endmodule

module Mem (
  input  wr,
  input  [31:0] MEM_WR,
  input  [31:0] MEM_ADDR_32,
  input  rd,
  input  [31:0] MEM_ADDR_8,
  input  fetch,
  input  CLK,
  output [31:0] MRM_RD,
  output [7:0] MEM_FETCH
);

  wire not_1_out, not_2_out, not_3_out;
  wire [7:0] ram_2_data;
  wire [31:0] ram_1_data;

  not not_1 (not_1_out, CLK);
  not not_2 (not_2_out, wr);
  RAM #(.addrWidth(24), .dataWidth(32)) ram_1 (
    .addr(MEM_ADDR_32[23:0]), .data(ram_1_data), .sel(1'b1), .clk(not_1_out), .ld(not_2_out), .clr(1'b0));
  assign ram_1_data = wr ? MEM_WR : 32'bz;  // Controlled_Buffer controlled_buffer_1
  assign MRM_RD = rd ? ram_1_data : 32'bz;  // Controlled_Buffer controlled_buffer_2
  not not_3 (not_3_out, CLK);
  assign MEM_FETCH = fetch ? ram_2_data : 8'bz;  // Controlled_Buffer controlled_buffer_3
  RAM #(.addrWidth(24)) ram_2 (
    .addr(MEM_ADDR_8[23:0]), .data(ram_2_data), .sel(1'b1), .clk(not_3_out), .clr(1'b0));  // open: ld

  // Notes on the sheet:
  //   Una truchada porque Logisim no tiene
  //   un bloque de memoria con dos canales de datos
endmodule

module Control_Unit (
  input  CLK,
  input  RESET,
  input  [7:0] MBR,
  input  N,
  input  Z,
  output [8:0] MPC,
  output MDR_B,
  output PC_B,
  output MBR_B,
  output MBRU_B,
  output SP_B,
  output LV_B,
  output CPP_B,
  output TOS_B,
  output OPC_B,
  output [2:0] Mem,
  output [5:0] ALU,
  output [1:0] Shifter,
  output H_C,
  output OPC_C,
  output TOS_C,
  output CPP_C,
  output LV_C,
  output SP_C,
  output PC_C,
  output MDR_C,
  output MAR_C
);

  wire and_1_out, and_2_out, d_flipflop_asc_1_p4, d_flipflop_asc_1_p5, d_flipflop_asc_2_p5;
  wire [2:0] mir_1_jam;
  wire [3:0] control_store_1_cs_s4, mir_1_b;
  wire [7:0] mir_1_addr, multiplexer_3_out, or_2_out;
  wire [8:0] multiplexer_1_out, multiplexer_2_out;
  wire [8:8] mir_1_addr_2, or_1_out;
  wire [31:0] control_store_1_cs_s32;

  Multiplexer #(.width(9), .enable("false")) multiplexer_1 (
    .in0({9{1'b1}}), .in1(9'hff), .out(multiplexer_1_out), .sel(RESET));
  Multiplexer #(.width(9), .enable("false")) multiplexer_2 (
    .in0({9{1'b1}}), .in1(9'h100), .out(multiplexer_2_out), .sel(RESET));
  and and_1 (and_1_out, d_flipflop_asc_1_p5, mir_1_jam[1]);
  // D_FlipFlop_Asc d_flipflop_asc_1: pin names not known; wires that end beside it: N, CLK, 1'b1, d_flipflop_asc_1_p4, d_flipflop_asc_1_p5
  // D_FlipFlop_Asc d_flipflop_asc_2: pin names not known; wires that end beside it: Z, CLK, 1'b1, d_flipflop_asc_1_p4, d_flipflop_asc_2_p5
  Multiplexer #(.width(8), .enable("false")) multiplexer_3 (
    .in0(mir_1_addr), .in1(or_2_out), .out(multiplexer_3_out), .sel(mir_1_jam[2]));
  or or_1 (or_1_out[8], and_1_out, and_2_out, mir_1_addr_2[8]);
  and and_2 (and_2_out, d_flipflop_asc_2_p5, mir_1_jam[0]);
  assign or_2_out = MBR | mir_1_addr;  // OR_Gate or_2, 8 bits wide
  not not_1 (d_flipflop_asc_1_p4, RESET);
  MPC mpc_1 (
    .Entrada({or_1_out[8], multiplexer_3_out}), .CLK(CLK), .Salida(MPC), .nPRE(multiplexer_1_out),
    .nCLR(multiplexer_2_out));
  Control_Store control_store_1 (.CS_E(MPC), .CS_S32(control_store_1_cs_s32), .CS_S4(control_store_1_cs_s4));
  MIR mir_1 (
    .Entrada_4(control_store_1_cs_s4), .Entrada_32(control_store_1_cs_s32), .CLK(CLK), .RESET(RESET),
    .B(mir_1_b), .Mem(Mem), .C({H_C, OPC_C, TOS_C, CPP_C, LV_C, SP_C, PC_C, MDR_C, MAR_C}),
    .ALU({Shifter, ALU}), .JAM(mir_1_jam), .Addr({mir_1_addr_2[8], mir_1_addr}));
  Decoder #(.select(4), .enable("false")) decoder_1 (
    .out0(MDR_B), .out1(PC_B), .out2(MBR_B), .out3(MBRU_B), .out4(SP_B), .out5(LV_B), .out6(CPP_B),
    .out7(TOS_B), .out8(OPC_B), .sel(mir_1_b));  // open: out9, out10, out11, out12, out13, out14, out15
endmodule

module Control_Store (
  input  [8:0] CS_E,
  output [31:0] CS_S32,
  output [3:0] CS_S4
);

  ROM #(.addrWidth(9), .dataWidth(32)) rom_1 (.addr(CS_E), .data(CS_S32), .sel(1'b1));
  ROM #(.addrWidth(9), .dataWidth(4)) rom_2 (.addr(CS_E), .data(CS_S4), .sel(1'b1));

  // Notes on the sheet:
  //   Otra truchada porque Logisim no tiene
  //   un bloque de memoria mas ancho que 32 bits
  //   contents of rom_1 (hex, n*v repeats v):
  //   80000000 255*0 435021
  //   contents of rom_2 (hex, n*v repeats v):
  //   f 255*0 1
endmodule

module MPC (
  input  [8:0] nPRE,
  input  [8:0] Entrada,
  input  CLK,
  input  [8:0] nCLR,
  output [8:0] Salida
);

  D_Latch d_latch_1 (.D(Entrada[8]), .CLK(CLK), .Q(Salida[8]), .nPRE(nPRE[8]), .nCLR(nCLR[8]));  // open: nQ
  D_Latch d_latch_2 (.D(Entrada[7]), .CLK(CLK), .Q(Salida[7]), .nPRE(nPRE[7]), .nCLR(nCLR[7]));  // open: nQ
  D_Latch d_latch_3 (.D(Entrada[6]), .CLK(CLK), .Q(Salida[6]), .nPRE(nPRE[6]), .nCLR(nCLR[6]));  // open: nQ
  D_Latch d_latch_4 (.D(Entrada[5]), .CLK(CLK), .Q(Salida[5]), .nPRE(nPRE[5]), .nCLR(nCLR[5]));  // open: nQ
  D_Latch d_latch_5 (.D(Entrada[4]), .CLK(CLK), .Q(Salida[4]), .nPRE(nPRE[4]), .nCLR(nCLR[4]));  // open: nQ
  D_Latch d_latch_6 (.D(Entrada[3]), .CLK(CLK), .Q(Salida[3]), .nPRE(nPRE[3]), .nCLR(nCLR[3]));  // open: nQ
  D_Latch d_latch_7 (.D(Entrada[2]), .CLK(CLK), .Q(Salida[2]), .nPRE(nPRE[2]), .nCLR(nCLR[2]));  // open: nQ
  D_Latch d_latch_8 (.D(Entrada[1]), .CLK(CLK), .Q(Salida[1]), .nPRE(nPRE[1]), .nCLR(nCLR[1]));  // open: nQ
  D_Latch d_latch_9 (.D(Entrada[0]), .CLK(CLK), .Q(Salida[0]), .nPRE(nPRE[0]), .nCLR(nCLR[0]));  // open: nQ
endmodule

module MIR (
  input  [3:0] Entrada_4,
  input  [31:0] Entrada_32,
  input  CLK,
  input  RESET,
  output [3:0] B,
  output [2:0] Mem,
  output [8:0] C,
  output [7:0] ALU,
  output [2:0] JAM,
  output [8:0] Addr
);

  wire [3:0] multiplexer_2_out, multiplexer_4_out, not_2_out;
  wire [31:0] multiplexer_1_out, multiplexer_3_out, not_1_out;

  Multiplexer #(.width(32), .enable("false")) multiplexer_1 (
    .in0({32{1'b1}}), .in1(not_1_out), .out(multiplexer_1_out), .sel(RESET));
  assign not_1_out = ~32'h435021;  // NOT_Gate not_1, 32 bits wide
  assign not_2_out = ~4'b0001;  // NOT_Gate not_2, 4 bits wide
  Multiplexer #(.width(4), .enable("false")) multiplexer_2 (
    .in0(4'b1111), .in1(not_2_out), .out(multiplexer_2_out), .sel(RESET));
  Multiplexer #(.width(32), .enable("false")) multiplexer_3 (
    .in0({32{1'b1}}), .in1(32'h435021), .out(multiplexer_3_out), .sel(RESET));
  Multiplexer #(.width(4), .enable("false")) multiplexer_4 (
    .in0(4'b1111), .in1(4'b0001), .out(multiplexer_4_out), .sel(RESET));
  Register_32_bits_Des register_32_bits_des_1 (
    .Entrada(Entrada_32), .CLK(CLK), .Salida({Addr, JAM, ALU, C, Mem}), .nPRE(multiplexer_1_out),
    .nCLR(multiplexer_3_out));
  Register_4_bits_Des register_4_bits_des_1 (
    .Entrada(Entrada_4), .CLK(CLK), .Salida(B), .nPRE(multiplexer_2_out), .nCLR(multiplexer_4_out));
endmodule

module Data_Path (
  input  MAR_C,
  input  [31:0] MEM_RD,
  input  MDR_B,
  input  MDR_C,
  input  rd,
  input  [7:0] MEM_FETCH,
  input  PC_B,
  input  PC_C,
  input  MBR,
  input  fetch,
  input  MBRU,
  input  SP_B,
  input  SP_C,
  input  LV_B,
  input  LV_C,
  input  CPP_B,
  input  CPP_C,
  input  RESET,
  input  TOS_B,
  input  TOS_C,
  input  OPC_B,
  input  OPC_C,
  input  H_C,
  input  INVA,
  input  ENA,
  input  CLK,
  input  ENB,
  input  INC,
  input  [1:0] F,
  input  SRA1,
  input  SLL8,
  output [31:0] MEM_MAR,
  output [31:0] MEM_WR,
  output [31:0] MEM_PC,
  output [7:0] OP_CODE,
  output [31:0] B,
  output N,
  output Z,
  output [31:0] C
);

  wire [7:0] multiplexer_1_out;
  wire [31:0] multiplexer_2_out;

  Multiplexer #(.width(8), .enable("false")) multiplexer_1 (
    .in0({8{1'b1}}), .in1({8{1'b0}}), .out(multiplexer_1_out), .sel(RESET));
  Multiplexer #(.width(32), .enable("false")) multiplexer_2 (
    .in0({32{1'b1}}), .in1({32{1'b0}}), .out(multiplexer_2_out), .sel(RESET));
  Multiplexer #(.width(32), .enable("false")) multiplexer_3 (.in0(C), .in1(MEM_RD), .sel(rd));  // open: out
  assign B = MDR_B ? MEM_WR : 32'bz;  // Controlled_Buffer controlled_buffer_1
  assign B = PC_B ? MEM_PC : 32'bz;  // Controlled_Buffer controlled_buffer_2
  MBR_EN mbr_en_1 (.in_1(OP_CODE), .Salida_Signada(B), .Salida_No_Signada(B), .MRB(MBR), .MBRU(MBRU));
  Controlled_Buffer #(.width(32)) controlled_buffer_3 (.out(B), .en(SP_B));  // open: in
  Controlled_Buffer #(.width(32)) controlled_buffer_4 (.out(B), .en(LV_B));  // open: in
  Controlled_Buffer #(.width(32)) controlled_buffer_5 (.out(B), .en(CPP_B));  // open: in
  Controlled_Buffer #(.width(32)) controlled_buffer_6 (.out(B), .en(TOS_B));  // open: in
  Controlled_Buffer #(.width(32)) controlled_buffer_7 (.out(B), .en(OPC_B));  // open: in

  // Notes on the sheet:
  //   Preset 8 Bits
  //   Clear 8 Bits
  //   Preset 32 Bits
  //   Clear 32 Bits
  //   Bus B
  //   Bus C
endmodule

module Register_32_bits_Hold___Paralel_Load (
  input  [31:0] nPRE,
  input  [31:0] Entrada,
  input  LOAD,
  input  CLK,
  input  [31:0] nCLR,
  output [31:0] Salida
);

  wire [31:0] multiplexer_1_out;

  Multiplexer #(.width(32), .enable("false")) multiplexer_1 (
    .in1(Entrada), .out(multiplexer_1_out), .sel(LOAD));  // open: in0
  D_FlipFlop_Des d_flipflop_des_1 (
    .D(multiplexer_1_out[31]), .CLK(CLK), .Q(Salida[31]), .nPRE(nPRE[31]), .nCLR(nCLR[31]));  // open: nQ
  D_FlipFlop_Des d_flipflop_des_2 (
    .D(multiplexer_1_out[30]), .CLK(CLK), .Q(Salida[30]), .nPRE(nPRE[30]), .nCLR(nCLR[30]));  // open: nQ
  D_FlipFlop_Des d_flipflop_des_3 (
    .D(multiplexer_1_out[29]), .CLK(CLK), .Q(Salida[29]), .nPRE(nPRE[29]), .nCLR(nCLR[29]));  // open: nQ
  D_FlipFlop_Des d_flipflop_des_4 (
    .D(multiplexer_1_out[28]), .CLK(CLK), .Q(Salida[28]), .nPRE(nPRE[28]), .nCLR(nCLR[28]));  // open: nQ
  D_FlipFlop_Des d_flipflop_des_5 (
    .D(multiplexer_1_out[27]), .CLK(CLK), .Q(Salida[27]), .nPRE(nPRE[27]), .nCLR(nCLR[27]));  // open: nQ
  D_FlipFlop_Des d_flipflop_des_6 (
    .D(multiplexer_1_out[26]), .CLK(CLK), .Q(Salida[26]), .nPRE(nPRE[26]), .nCLR(nCLR[26]));  // open: nQ
  D_FlipFlop_Des d_flipflop_des_7 (
    .D(multiplexer_1_out[25]), .CLK(CLK), .Q(Salida[25]), .nPRE(nPRE[25]), .nCLR(nCLR[25]));  // open: nQ
  D_FlipFlop_Des d_flipflop_des_8 (
    .D(multiplexer_1_out[24]), .CLK(CLK), .Q(Salida[24]), .nPRE(nPRE[24]), .nCLR(nCLR[24]));  // open: nQ
  D_FlipFlop_Des d_flipflop_des_9 (
    .D(multiplexer_1_out[23]), .CLK(CLK), .Q(Salida[23]), .nPRE(nPRE[23]), .nCLR(nCLR[23]));  // open: nQ
  D_FlipFlop_Des d_flipflop_des_10 (
    .D(multiplexer_1_out[22]), .CLK(CLK), .Q(Salida[22]), .nPRE(nPRE[22]), .nCLR(nCLR[22]));  // open: nQ
  D_FlipFlop_Des d_flipflop_des_11 (
    .D(multiplexer_1_out[21]), .CLK(CLK), .Q(Salida[21]), .nPRE(nPRE[21]), .nCLR(nCLR[21]));  // open: nQ
  D_FlipFlop_Des d_flipflop_des_12 (
    .D(multiplexer_1_out[20]), .CLK(CLK), .Q(Salida[20]), .nPRE(nPRE[20]), .nCLR(nCLR[20]));  // open: nQ
  D_FlipFlop_Des d_flipflop_des_13 (
    .D(multiplexer_1_out[19]), .CLK(CLK), .Q(Salida[19]), .nPRE(nPRE[19]), .nCLR(nCLR[19]));  // open: nQ
  D_FlipFlop_Des d_flipflop_des_14 (
    .D(multiplexer_1_out[18]), .CLK(CLK), .Q(Salida[18]), .nPRE(nPRE[18]), .nCLR(nCLR[18]));  // open: nQ
  D_FlipFlop_Des d_flipflop_des_15 (
    .D(multiplexer_1_out[17]), .CLK(CLK), .Q(Salida[17]), .nPRE(nPRE[17]), .nCLR(nCLR[17]));  // open: nQ
  D_FlipFlop_Des d_flipflop_des_16 (
    .D(multiplexer_1_out[16]), .CLK(CLK), .Q(Salida[16]), .nPRE(nPRE[16]), .nCLR(nCLR[16]));  // open: nQ
  D_FlipFlop_Des d_flipflop_des_17 (
    .D(multiplexer_1_out[15]), .CLK(CLK), .Q(Salida[15]), .nPRE(nPRE[15]), .nCLR(nCLR[15]));  // open: nQ
  D_FlipFlop_Des d_flipflop_des_18 (
    .D(multiplexer_1_out[14]), .CLK(CLK), .Q(Salida[14]), .nPRE(nPRE[14]), .nCLR(nCLR[14]));  // open: nQ
  D_FlipFlop_Des d_flipflop_des_19 (
    .D(multiplexer_1_out[13]), .CLK(CLK), .Q(Salida[13]), .nPRE(nPRE[13]), .nCLR(nCLR[13]));  // open: nQ
  D_FlipFlop_Des d_flipflop_des_20 (
    .D(multiplexer_1_out[12]), .CLK(CLK), .Q(Salida[12]), .nPRE(nPRE[12]), .nCLR(nCLR[12]));  // open: nQ
  D_FlipFlop_Des d_flipflop_des_21 (
    .D(multiplexer_1_out[11]), .CLK(CLK), .Q(Salida[11]), .nPRE(nPRE[11]), .nCLR(nCLR[11]));  // open: nQ
  D_FlipFlop_Des d_flipflop_des_22 (
    .D(multiplexer_1_out[10]), .CLK(CLK), .Q(Salida[10]), .nPRE(nPRE[10]), .nCLR(nCLR[10]));  // open: nQ
  D_FlipFlop_Des d_flipflop_des_23 (
    .D(multiplexer_1_out[9]), .CLK(CLK), .Q(Salida[9]), .nPRE(nPRE[9]), .nCLR(nCLR[9]));  // open: nQ
  D_FlipFlop_Des d_flipflop_des_24 (
    .D(multiplexer_1_out[8]), .CLK(CLK), .Q(Salida[8]), .nPRE(nPRE[8]), .nCLR(nCLR[8]));  // open: nQ
  D_FlipFlop_Des d_flipflop_des_25 (
    .D(multiplexer_1_out[7]), .CLK(CLK), .Q(Salida[7]), .nPRE(nPRE[7]), .nCLR(nCLR[7]));  // open: nQ
  D_FlipFlop_Des d_flipflop_des_26 (
    .D(multiplexer_1_out[6]), .CLK(CLK), .Q(Salida[6]), .nPRE(nPRE[6]), .nCLR(nCLR[6]));  // open: nQ
  D_FlipFlop_Des d_flipflop_des_27 (
    .D(multiplexer_1_out[5]), .CLK(CLK), .Q(Salida[5]), .nPRE(nPRE[5]), .nCLR(nCLR[5]));  // open: nQ
  D_FlipFlop_Des d_flipflop_des_28 (
    .D(multiplexer_1_out[4]), .CLK(CLK), .Q(Salida[4]), .nPRE(nPRE[4]), .nCLR(nCLR[4]));  // open: nQ
  D_FlipFlop_Des d_flipflop_des_29 (
    .D(multiplexer_1_out[3]), .CLK(CLK), .Q(Salida[3]), .nPRE(nPRE[3]), .nCLR(nCLR[3]));  // open: nQ
  D_FlipFlop_Des d_flipflop_des_30 (
    .D(multiplexer_1_out[2]), .CLK(CLK), .Q(Salida[2]), .nPRE(nPRE[2]), .nCLR(nCLR[2]));  // open: nQ
  D_FlipFlop_Des d_flipflop_des_31 (
    .D(multiplexer_1_out[1]), .CLK(CLK), .Q(Salida[1]), .nPRE(nPRE[1]), .nCLR(nCLR[1]));  // open: nQ
  D_FlipFlop_Des d_flipflop_des_32 (
    .D(multiplexer_1_out[0]), .CLK(CLK), .Q(Salida[0]), .nPRE(nPRE[0]), .nCLR(nCLR[0]));  // open: nQ
endmodule

module Register_32_bits_Des (
  input  [31:0] nPRE,
  input  [31:0] Entrada,
  input  CLK,
  input  [31:0] nCLR,
  output [31:0] Salida
);

  D_FlipFlop_Des d_flipflop_des_1 (
    .D(Entrada[31]), .CLK(CLK), .Q(Salida[31]), .nPRE(nPRE[31]), .nCLR(nCLR[31]));  // open: nQ
  D_FlipFlop_Des d_flipflop_des_2 (
    .D(Entrada[30]), .CLK(CLK), .Q(Salida[30]), .nPRE(nPRE[30]), .nCLR(nCLR[30]));  // open: nQ
  D_FlipFlop_Des d_flipflop_des_3 (
    .D(Entrada[29]), .CLK(CLK), .Q(Salida[29]), .nPRE(nPRE[29]), .nCLR(nCLR[29]));  // open: nQ
  D_FlipFlop_Des d_flipflop_des_4 (
    .D(Entrada[28]), .CLK(CLK), .Q(Salida[28]), .nPRE(nPRE[28]), .nCLR(nCLR[28]));  // open: nQ
  D_FlipFlop_Des d_flipflop_des_5 (
    .D(Entrada[27]), .CLK(CLK), .Q(Salida[27]), .nPRE(nPRE[27]), .nCLR(nCLR[27]));  // open: nQ
  D_FlipFlop_Des d_flipflop_des_6 (
    .D(Entrada[26]), .CLK(CLK), .Q(Salida[26]), .nPRE(nPRE[26]), .nCLR(nCLR[26]));  // open: nQ
  D_FlipFlop_Des d_flipflop_des_7 (
    .D(Entrada[25]), .CLK(CLK), .Q(Salida[25]), .nPRE(nPRE[25]), .nCLR(nCLR[25]));  // open: nQ
  D_FlipFlop_Des d_flipflop_des_8 (
    .D(Entrada[24]), .CLK(CLK), .Q(Salida[24]), .nPRE(nPRE[24]), .nCLR(nCLR[24]));  // open: nQ
  D_FlipFlop_Des d_flipflop_des_9 (
    .D(Entrada[23]), .CLK(CLK), .Q(Salida[23]), .nPRE(nPRE[23]), .nCLR(nCLR[23]));  // open: nQ
  D_FlipFlop_Des d_flipflop_des_10 (
    .D(Entrada[22]), .CLK(CLK), .Q(Salida[22]), .nPRE(nPRE[22]), .nCLR(nCLR[22]));  // open: nQ
  D_FlipFlop_Des d_flipflop_des_11 (
    .D(Entrada[21]), .CLK(CLK), .Q(Salida[21]), .nPRE(nPRE[21]), .nCLR(nCLR[21]));  // open: nQ
  D_FlipFlop_Des d_flipflop_des_12 (
    .D(Entrada[20]), .CLK(CLK), .Q(Salida[20]), .nPRE(nPRE[20]), .nCLR(nCLR[20]));  // open: nQ
  D_FlipFlop_Des d_flipflop_des_13 (
    .D(Entrada[19]), .CLK(CLK), .Q(Salida[19]), .nPRE(nPRE[19]), .nCLR(nCLR[19]));  // open: nQ
  D_FlipFlop_Des d_flipflop_des_14 (
    .D(Entrada[18]), .CLK(CLK), .Q(Salida[18]), .nPRE(nPRE[18]), .nCLR(nCLR[18]));  // open: nQ
  D_FlipFlop_Des d_flipflop_des_15 (
    .D(Entrada[17]), .CLK(CLK), .Q(Salida[17]), .nPRE(nPRE[17]), .nCLR(nCLR[17]));  // open: nQ
  D_FlipFlop_Des d_flipflop_des_16 (
    .D(Entrada[16]), .CLK(CLK), .Q(Salida[16]), .nPRE(nPRE[16]), .nCLR(nCLR[16]));  // open: nQ
  D_FlipFlop_Des d_flipflop_des_17 (
    .D(Entrada[15]), .CLK(CLK), .Q(Salida[15]), .nPRE(nPRE[15]), .nCLR(nCLR[15]));  // open: nQ
  D_FlipFlop_Des d_flipflop_des_18 (
    .D(Entrada[14]), .CLK(CLK), .Q(Salida[14]), .nPRE(nPRE[14]), .nCLR(nCLR[14]));  // open: nQ
  D_FlipFlop_Des d_flipflop_des_19 (
    .D(Entrada[13]), .CLK(CLK), .Q(Salida[13]), .nPRE(nPRE[13]), .nCLR(nCLR[13]));  // open: nQ
  D_FlipFlop_Des d_flipflop_des_20 (
    .D(Entrada[12]), .CLK(CLK), .Q(Salida[12]), .nPRE(nPRE[12]), .nCLR(nCLR[12]));  // open: nQ
  D_FlipFlop_Des d_flipflop_des_21 (
    .D(Entrada[11]), .CLK(CLK), .Q(Salida[11]), .nPRE(nPRE[11]), .nCLR(nCLR[11]));  // open: nQ
  D_FlipFlop_Des d_flipflop_des_22 (
    .D(Entrada[10]), .CLK(CLK), .Q(Salida[10]), .nPRE(nPRE[10]), .nCLR(nCLR[10]));  // open: nQ
  D_FlipFlop_Des d_flipflop_des_23 (
    .D(Entrada[9]), .CLK(CLK), .Q(Salida[9]), .nPRE(nPRE[9]), .nCLR(nCLR[9]));  // open: nQ
  D_FlipFlop_Des d_flipflop_des_24 (
    .D(Entrada[8]), .CLK(CLK), .Q(Salida[8]), .nPRE(nPRE[8]), .nCLR(nCLR[8]));  // open: nQ
  D_FlipFlop_Des d_flipflop_des_25 (
    .D(Entrada[7]), .CLK(CLK), .Q(Salida[7]), .nPRE(nPRE[7]), .nCLR(nCLR[7]));  // open: nQ
  D_FlipFlop_Des d_flipflop_des_26 (
    .D(Entrada[6]), .CLK(CLK), .Q(Salida[6]), .nPRE(nPRE[6]), .nCLR(nCLR[6]));  // open: nQ
  D_FlipFlop_Des d_flipflop_des_27 (
    .D(Entrada[5]), .CLK(CLK), .Q(Salida[5]), .nPRE(nPRE[5]), .nCLR(nCLR[5]));  // open: nQ
  D_FlipFlop_Des d_flipflop_des_28 (
    .D(Entrada[4]), .CLK(CLK), .Q(Salida[4]), .nPRE(nPRE[4]), .nCLR(nCLR[4]));  // open: nQ
  D_FlipFlop_Des d_flipflop_des_29 (
    .D(Entrada[3]), .CLK(CLK), .Q(Salida[3]), .nPRE(nPRE[3]), .nCLR(nCLR[3]));  // open: nQ
  D_FlipFlop_Des d_flipflop_des_30 (
    .D(Entrada[2]), .CLK(CLK), .Q(Salida[2]), .nPRE(nPRE[2]), .nCLR(nCLR[2]));  // open: nQ
  D_FlipFlop_Des d_flipflop_des_31 (
    .D(Entrada[1]), .CLK(CLK), .Q(Salida[1]), .nPRE(nPRE[1]), .nCLR(nCLR[1]));  // open: nQ
  D_FlipFlop_Des d_flipflop_des_32 (
    .D(Entrada[0]), .CLK(CLK), .Q(Salida[0]), .nPRE(nPRE[0]), .nCLR(nCLR[0]));  // open: nQ
endmodule

module Register_8_bits_Hold___Paralel_Load (
  input  [7:0] nPRE,
  input  [7:0] Entrada,
  input  LOAD,
  input  CLK,
  input  [7:0] nCLR,
  output Q,
  output Q_2,
  output Q_3,
  output Q_4,
  output nQ,
  output nQ_2,
  output nQ_3,
  output nQ_4,
  output [7:0] Salida,
  output Q_5,
  output Q_6,
  output Q_7,
  output Q_8,
  output nQ_5,
  output nQ_6,
  output nQ_7,
  output nQ_8
);

  wire nand_1_out, nand_2_out, nand_3_out, nand_4_out, nand_5_out, nand_6_out, nand_7_out, nand_8_out,
       nand_9_out, nand_10_out, nand_11_out, nand_12_out, nand_17_out, nand_18_out, nand_19_out, nand_20_out,
       nand_21_out, nand_22_out, nand_23_out, nand_24_out, nand_25_out, nand_26_out, nand_29_out,
       nand_30_out, nand_33_out, nand_34_out, nand_35_out, nand_36_out, nand_37_out, nand_38_out,
       nand_39_out, nand_40_out, nand_41_out, nand_42_out, nand_43_out, nand_44_out, nand_49_out,
       nand_50_out, nand_51_out, nand_52_out, nand_53_out, nand_54_out, nand_55_out, nand_56_out,
       nand_57_out, nand_58_out, nand_59_out, nand_60_out, not_1_out, not_2_out, not_3_out, not_4_out,
       not_5_out, not_6_out, not_7_out, not_8_out, not_9_out, not_10_out, not_11_out, not_12_out, not_13_out,
       not_14_out, not_15_out, not_16_out, undriven, undriven_2, undriven_3, undriven_4, undriven_5,
       undriven_6, undriven_7;
  wire [7:0] multiplexer_1_out;

  Multiplexer #(.width(8), .enable("false")) multiplexer_1 (
    .in1(Entrada), .out(multiplexer_1_out), .sel(LOAD));  // open: in0
  not not_1 (not_1_out, multiplexer_1_out[0]);
  not not_2 (not_2_out, multiplexer_1_out[4]);
  nand nand_1 (nand_1_out, nQ_3, multiplexer_1_out[0], CLK);
  nand nand_2 (nand_2_out, CLK, not_1_out, Q_3);
  not not_3 (not_3_out, CLK);
  not not_4 (not_4_out, CLK);
  nand nand_3 (nand_3_out, nPRE[0], nand_1_out, nand_4_out);
  nand nand_4 (nand_4_out, nand_3_out, nand_2_out, undriven);
  nand nand_5 (nand_5_out, nQ_7, multiplexer_1_out[4], CLK);
  nand nand_6 (nand_6_out, CLK, not_2_out, Q_7);
  nand nand_7 (nand_7_out, nPRE[4], nand_5_out, nand_8_out);
  nand nand_8 (nand_8_out, nand_7_out, nand_6_out, undriven_2);
  nand nand_9 (nand_9_out, nand_3_out, not_3_out);
  nand nand_10 (nand_10_out, not_3_out, nand_4_out);
  nand nand_11 (nand_11_out, nand_7_out, not_4_out);
  nand nand_12 (nand_12_out, not_4_out, nand_8_out);
  nand nand_13 (Q_3, nPRE[0], nand_9_out, nQ_3);
  nand nand_14 (nQ_3, Q_3, nand_10_out, undriven);
  nand nand_15 (Q_7, nPRE[4], nand_11_out, nQ_7);
  nand nand_16 (nQ_7, Q_7, nand_12_out, undriven_2);
  not not_5 (not_5_out, multiplexer_1_out[1]);
  not not_6 (not_6_out, CLK);
  not not_7 (not_7_out, multiplexer_1_out[5]);
  nand nand_17 (nand_17_out, nQ, multiplexer_1_out[1], CLK);
  nand nand_18 (nand_18_out, CLK, not_5_out, Q);
  nand nand_19 (nand_19_out, nQ_5, multiplexer_1_out[5], CLK);
  nand nand_20 (nand_20_out, CLK, not_7_out, Q_5);
  not not_8 (not_8_out, CLK);
  nand nand_21 (nand_21_out, nPRE[1], nand_17_out, nand_22_out);
  nand nand_22 (nand_22_out, nand_21_out, nand_18_out, undriven_3);
  nand nand_23 (nand_23_out, nPRE[5], nand_19_out, nand_24_out);
  nand nand_24 (nand_24_out, nand_23_out, nand_20_out, undriven_4);
  nand nand_25 (nand_25_out, nand_21_out, not_6_out);
  nand nand_26 (nand_26_out, not_6_out, nand_22_out);
  nand nand_27 (Q, nPRE[1], nand_25_out, nQ);
  nand nand_28 (nQ, Q, nand_26_out, undriven_3);
  nand nand_29 (nand_29_out, nand_23_out, not_8_out);
  nand nand_30 (nand_30_out, not_8_out, nand_24_out);
  nand nand_31 (Q_5, nPRE[5], nand_29_out, nQ_5);
  nand nand_32 (nQ_5, Q_5, nand_30_out, undriven_4);
  not not_9 (not_9_out, multiplexer_1_out[2]);
  not not_10 (not_10_out, CLK);
  not not_11 (not_11_out, multiplexer_1_out[6]);
  nand nand_33 (nand_33_out, nQ_4, multiplexer_1_out[2], CLK);
  nand nand_34 (nand_34_out, CLK, not_9_out, Q_4);
  nand nand_35 (nand_35_out, nQ_8, multiplexer_1_out[6], CLK);
  nand nand_36 (nand_36_out, CLK, not_11_out, Q_8);
  not not_12 (not_12_out, CLK);
  nand nand_37 (nand_37_out, nPRE[2], nand_33_out, nand_38_out);
  nand nand_38 (nand_38_out, nand_37_out, nand_34_out, undriven_5);
  nand nand_39 (nand_39_out, nPRE[6], nand_35_out, nand_40_out);
  nand nand_40 (nand_40_out, nand_39_out, nand_36_out, undriven_6);
  nand nand_41 (nand_41_out, nand_37_out, not_10_out);
  nand nand_42 (nand_42_out, not_10_out, nand_38_out);
  nand nand_43 (nand_43_out, nand_39_out, not_12_out);
  nand nand_44 (nand_44_out, not_12_out, nand_40_out);
  nand nand_45 (Q_4, nPRE[2], nand_41_out, nQ_4);
  nand nand_46 (nQ_4, Q_4, nand_42_out, undriven_5);
  nand nand_47 (Q_8, nPRE[6], nand_43_out, nQ_8);
  nand nand_48 (nQ_8, Q_8, nand_44_out, undriven_6);
  not not_13 (not_13_out, multiplexer_1_out[3]);
  not not_14 (not_14_out, CLK);
  not not_15 (not_15_out, multiplexer_1_out[7]);
  not not_16 (not_16_out, CLK);
  nand nand_49 (nand_49_out, nQ_2, multiplexer_1_out[3], CLK);
  nand nand_50 (nand_50_out, CLK, not_13_out, Q_2);
  nand nand_51 (nand_51_out, nQ_6, multiplexer_1_out[7], CLK);
  nand nand_52 (nand_52_out, CLK, not_15_out, Q_6);
  nand nand_53 (nand_53_out, nPRE[3], nand_49_out, nand_54_out);
  nand nand_54 (nand_54_out, nand_53_out, nand_50_out, undriven_7);
  nand nand_55 (nand_55_out, nPRE[7], nand_51_out, nand_56_out);
  nand nand_56 (nand_56_out, nand_55_out, nand_52_out, nCLR[7]);
  nand nand_57 (nand_57_out, nand_53_out, not_14_out);
  nand nand_58 (nand_58_out, not_14_out, nand_54_out);
  nand nand_59 (nand_59_out, nand_55_out, not_16_out);
  nand nand_60 (nand_60_out, not_16_out, nand_56_out);
  nand nand_61 (Q_2, nPRE[3], nand_57_out, nQ_2);
  nand nand_62 (nQ_2, Q_2, nand_58_out, undriven_7);
  nand nand_63 (Q_6, nPRE[7], nand_59_out, nQ_6);
  nand nand_64 (nQ_6, Q_6, nand_60_out, nCLR[7]);

  assign Salida = {Q_6, Q_8, Q_5, Q_7, Q_2, Q_4, Q, Q_3};
endmodule

module Register_4_bits_Des (
  input  [3:0] nPRE,
  input  [3:0] Entrada,
  input  CLK,
  input  [3:0] nCLR,
  output [3:0] Salida
);

  D_FlipFlop_Des d_flipflop_des_1 (
    .D(Entrada[3]), .CLK(CLK), .Q(Salida[3]), .nPRE(nPRE[3]), .nCLR(nCLR[3]));  // open: nQ
  D_FlipFlop_Des d_flipflop_des_2 (
    .D(Entrada[2]), .CLK(CLK), .Q(Salida[2]), .nPRE(nPRE[2]), .nCLR(nCLR[2]));  // open: nQ
  D_FlipFlop_Des d_flipflop_des_3 (
    .D(Entrada[1]), .CLK(CLK), .Q(Salida[1]), .nPRE(nPRE[1]), .nCLR(nCLR[1]));  // open: nQ
  D_FlipFlop_Des d_flipflop_des_4 (
    .D(Entrada[0]), .CLK(CLK), .Q(Salida[0]), .nPRE(nPRE[0]), .nCLR(nCLR[0]));  // open: nQ
endmodule

module MBR_EN (
  input  [7:0] in_1,
  input  MRB,
  input  MBRU,
  output [31:0] Salida_Signada,
  output [31:0] Salida_No_Signada
);

  assign Salida_Signada = MRB ? {{25{in_1[7]}}, in_1[6:0]} : 32'bz;  // Controlled_Buffer controlled_buffer_1
  assign Salida_No_Signada = MBRU ? {{24{1'b0}}, in_1} : 32'bz;  // Controlled_Buffer controlled_buffer_2
endmodule

module D_FlipFlop_Des (
  input  nPRE,
  input  D,
  input  CLK,
  input  nCLR,
  output Q,
  output nQ
);

  wire d_latch_1_q, not_1_out;

  D_Latch d_latch_1 (.D(D), .CLK(CLK), .Q(d_latch_1_q), .nPRE(nPRE), .nCLR(nCLR));  // open: nQ
  not not_1 (not_1_out, CLK);
  D_Latch d_latch_2 (.D(d_latch_1_q), .CLK(not_1_out), .Q(Q), .nQ(nQ), .nPRE(nPRE), .nCLR(nCLR));
endmodule

module D_FlipFlop_Asc (
  input  nPRE,
  input  D,
  input  CLK,
  input  nCLR,
  output Q,
  output nQ
);

  wire d_latch_1_q, not_1_out;

  not not_1 (not_1_out, CLK);
  D_Latch d_latch_1 (.D(D), .CLK(not_1_out), .Q(d_latch_1_q), .nPRE(nPRE), .nCLR(nCLR));  // open: nQ
  D_Latch d_latch_2 (.D(d_latch_1_q), .CLK(CLK), .Q(Q), .nQ(nQ), .nPRE(nPRE), .nCLR(nCLR));
endmodule

module D_Latch (
  input  nPRE,
  input  D,
  input  CLK,
  input  nCLR,
  output Q,
  output nQ
);
endmodule

module ALU_1_bit (
  input  Cin,
  input  INVA,
  input  A,
  input  ENA,
  input  B,
  input  ENB,
  input  [1:0] F,
  output Salida,
  output Cout
);
endmodule

module Unidad_Logica__ALU (
  input  A,
  input  B,
  input  EN1,
  input  EN2,
  input  EN3,
  output AND,
  output OR,
  output NOT
);
endmodule

module Sumador_Completo__ALU (
  input  Cin,
  input  A,
  input  B,
  input  EN,
  output S,
  output Cout
);
endmodule

module Desplazador (
  input  [31:0] Entrada,
  input  SRA1,
  input  SLL8,
  output [31:0] Salida
);
endmodule
